// Logisim project dflipflop.circ as structural Verilog: 1 circuit, main circuit main
module main (
);

  wire button_1_out, button_2_out, button_3_out, button_4_out, d_ff_1_q, d_ff_1_qn, nor_1_out, nor_2_out,
       R_out, S_out;

  Button S (.out(S_out));
  Button R (.out(R_out));
  Button button_1 (.out(button_1_out));
  Button button_2 (.out(button_2_out));
  Button button_3 (.out(button_3_out));
  D_Flip_Flop d_ff_1 (
    .D(button_1_out), .clk(button_2_out), .Q(d_ff_1_q), .Qn(d_ff_1_qn), .preset(button_3_out),
    .reset(button_4_out));
  Button button_4 (.out(button_4_out));
  DipSwitch dipswitch_1 ();  // open: sw1, sw2, sw3, sw4, sw5, sw6, sw7, sw8
  nor nor_1 (nor_1_out, S_out, nor_2_out);
  LED Q (.in(nor_1_out));
  nor nor_2 (nor_2_out, R_out, nor_1_out);
  LED MINUSQ (.in(nor_2_out));
  LED led_1 (.in(d_ff_1_q));
  LED led_2 (.in(d_ff_1_qn));
endmodule
