// Logisim project ersteschaltung.circ as structural Verilog: 1 circuit, main circuit main
module main (
);

  wire and_1_out, dipswitch_1_sw1, dipswitch_1_sw2, xor_1_out;

  Button A ();  // open: out
  DipSwitch dipswitch_1 (.sw1(dipswitch_1_sw1), .sw2(dipswitch_1_sw2));  // open: sw3, sw4, sw5, sw6, sw7, sw8
  xor xor_1 (xor_1_out, dipswitch_1_sw1, dipswitch_1_sw2);
  LED S (.in(xor_1_out));
  and and_1 (and_1_out, dipswitch_1_sw1, dipswitch_1_sw2);
  LED C (.in(and_1_out));
  Button B ();  // open: out
endmodule
